// Logisim project Pipelined MIPS.circ as structural Verilog: 19 circuits, main circuit MIPS32
module MIPS32 (
);

  wire and_1_out, branch_1_branch, clock_1_out, EMWE_q, exhazard_1_fa, exhazard_1_fb, J_q, jandb_1_j,
       memhazard_1_fa, memhazard_1_fb, memsel_1_ld, memsel_1_str, multiplexer_7_out, nor_1_out, or_1_out,
       or_2_out, register_2_q, register_3_q, registerfile_1_p3, stall_1_stalling, stalling_q, wesel_1_we;
  wire [3:0] aludecode_1_aluop, ALUop_q, memsel_1_sel;
  wire [4:0] control_1_ra, control_1_rb, control_1_rw, EMrd_q, IErs_q, IErt_q, registerfile_1_p4, rW_q,
       shamt_q;
  wire [19:0] memin_1_a;
  wire [31:0] alu_1_c, alu_1_w, bit_extender_1_out, bit_extender_2_out, bit_extender_3_out, IEPC_q, Imme_q,
       jandb_1_npc, loadsel_1_w, memin_1_d, mips_ram_1_p7, MIPSop_q, mipsprogramrom_1_p1,
       mipsprogramrom_1_p2, multiplexer_1_out, multiplexer_2_out, multiplexer_3_out, multiplexer_4_out,
       multiplexer_5_out, multiplexer_6_out, register_1_q, register_4_q, register_5_q, register_6_q,
       register_7_q, registerfile_1_p1, registerfile_1_p7, registerfile_1_p8, signedoff_q, store_q;

  Clock clock_1 (.out(clock_1_out));
  // MIPSProgramROM mipsprogramrom_1: pin names not known; wires that end beside it: mipsprogramrom_1_p1, mipsprogramrom_1_p2
  JandB jandb_1 (
    .PC(mipsprogramrom_1_p1), .signedoff(signedoff_q), .rs(multiplexer_5_out), .Branch(branch_1_branch),
    .MIPSop(MIPSop_q), .stalling(stall_1_stalling), .OldJ(J_q), .NPC(jandb_1_npc), .J(jandb_1_j));  // open: WE
  assign bit_extender_1_out = {{31{1'b0}}, mipsprogramrom_1_p2[30]};  // Bit_Extender bit_extender_1
  stall stall_1 (
    .MIPSop(register_1_q), .FDrs(mipsprogramrom_1_p2[25:21]), .IErt(control_1_rb),
    .FDrt(mipsprogramrom_1_p2[20:16]), .stalling(stall_1_stalling));
  Multiplexer #(.width(32), .enable("false")) multiplexer_1 (
    .in0(mipsprogramrom_1_p2), .in1(bit_extender_1_out), .out(multiplexer_1_out), .sel(stall_1_stalling));
  Register #(.width(32)) register_1 (.D(multiplexer_1_out), .clk(clock_1_out), .Q(register_1_q));  // open: en, clr
  Register #(.width(32)) PC (.D(jandb_1_npc), .clk(clock_1_out), .Q(mipsprogramrom_1_p1));  // open: en, clr
  Register #(.width(1)) register_2 (.D(jandb_1_j), .clk(clock_1_out), .Q(register_2_q));  // open: en, clr
  Register #(.width(1)) register_3 (.D(stall_1_stalling), .clk(clock_1_out), .Q(register_3_q));  // open: en, clr
  control control_1 (.MIPSop(register_1_q), .rB(control_1_rb), .rA(control_1_ra), .rW(control_1_rw));
  ALUdecode aludecode_1 (.MIPSop(register_1_q), .ALUop(aludecode_1_aluop));
  assign bit_extender_2_out = {{16{register_1_q[15]}}, register_1_q[15:0]};  // Bit_Extender bit_extender_2
  assign bit_extender_3_out = {{16{1'b0}}, register_1_q[15:0]};  // Bit_Extender bit_extender_3
  // RegisterFile #(.trigger("falling")) registerfile_1: pin names not known; wires that end beside it: registerfile_1_p1, clock_1_out, registerfile_1_p3, registerfile_1_p4, control_1_ra, control_1_rb, registerfile_1_p7, registerfile_1_p8
  Multiplexer #(.width(32), .enable("false")) multiplexer_2 (
    .in0(bit_extender_2_out), .in1(bit_extender_3_out), .out(multiplexer_2_out), .sel(register_1_q[28]));
  Register #(.width(32)) register_4 (.D(registerfile_1_p7), .clk(clock_1_out), .Q(register_4_q));  // open: en, clr
  Register #(.width(32)) register_5 (.D(registerfile_1_p8), .clk(clock_1_out), .Q(register_5_q));  // open: en, clr
  Register #(.width(32)) IEPC (.D(mipsprogramrom_1_p1), .clk(clock_1_out), .Q(IEPC_q));  // open: en, clr
  Register #(.width(5)) rW (.D(control_1_rw), .clk(clock_1_out), .Q(rW_q));  // open: en, clr
  Register #(.width(32)) MIPSop (.D(register_1_q), .clk(clock_1_out), .Q(MIPSop_q));  // open: en, clr
  Register #(.width(4)) ALUop (.D(aludecode_1_aluop), .clk(clock_1_out), .Q(ALUop_q));  // open: en, clr
  Register #(.width(5)) IErs (.D(control_1_ra), .clk(clock_1_out), .Q(IErs_q));  // open: en, clr
  Register #(.width(5)) IErt (.D(control_1_rb), .clk(clock_1_out), .Q(IErt_q));  // open: en, clr
  Register #(.width(1)) stalling (.D(register_3_q), .clk(clock_1_out), .Q(stalling_q));  // open: en, clr
  Register #(.width(1)) J (.D(register_2_q), .clk(clock_1_out), .Q(J_q));  // open: en, clr
  Register #(.width(32)) Imme (.D(multiplexer_2_out), .clk(clock_1_out), .Q(Imme_q));  // open: en, clr
  Register #(.width(32)) signedoff (.D(bit_extender_2_out), .clk(clock_1_out), .Q(signedoff_q));  // open: en, clr
  Register #(.width(5)) shamt (.D(register_1_q[10:6]), .clk(clock_1_out), .Q(shamt_q));  // open: en, clr
  Multiplexer #(.width(32), .enable("false")) multiplexer_3 (
    .in0(registerfile_1_p1), .in1(register_6_q), .out(multiplexer_3_out), .sel(exhazard_1_fa));
  Multiplexer #(.width(32), .enable("false")) multiplexer_4 (
    .in0(registerfile_1_p1), .in1(register_6_q), .out(multiplexer_4_out), .sel(exhazard_1_fb));
  Multiplexer #(.width(32), .enable("false")) multiplexer_5 (
    .in0(register_4_q), .in1(multiplexer_3_out), .out(multiplexer_5_out), .sel(or_1_out));
  or or_1 (or_1_out, memhazard_1_fa, exhazard_1_fa);
  Multiplexer #(.width(32), .enable("false")) multiplexer_6 (
    .in0(register_5_q), .in1(multiplexer_4_out), .out(multiplexer_6_out), .sel(or_2_out));
  or or_2 (or_2_out, memhazard_1_fb, exhazard_1_fb);
  EXhazard exhazard_1 (
    .EMWE(EMWE_q), .EMrd(EMrd_q), .IErs(IErs_q), .IErt(IErt_q), .FA(exhazard_1_fa), .FB(exhazard_1_fb));
  MEMhazard memhazard_1 (
    .MWWE(registerfile_1_p3), .MWrd(registerfile_1_p4), .IErs(IErs_q), .IErt(IErt_q), .EMWE(EMWE_q),
    .EMrd(EMrd_q), .FA(memhazard_1_fa), .FB(memhazard_1_fb));
  ALU alu_1 (
    .A(multiplexer_5_out), .B(multiplexer_6_out), .op(ALUop_q), .imme(Imme_q), .shamt(shamt_q),
    .MIPSop(MIPSop_q), .PC(IEPC_q), .C(alu_1_c), .W(alu_1_w));
  Branch branch_1 (.MIPSop(MIPSop_q), .A(multiplexer_5_out), .B(multiplexer_6_out), .Branch(branch_1_branch));
  WEsel wesel_1 (.C(alu_1_c), .MIPSop(MIPSop_q), .stalling(stalling_q), .J(J_q), .WE(wesel_1_we));
  Register #(.width(32)) register_6 (.D(alu_1_w), .clk(clock_1_out), .Q(register_6_q));  // open: en, clr
  Register #(.width(32)) store (.D(multiplexer_6_out), .clk(clock_1_out), .Q(store_q));  // open: en, clr
  Register #(.width(5)) EMrd (.D(rW_q), .clk(clock_1_out), .Q(EMrd_q));  // open: en, clr
  Register #(.width(32)) register_7 (.D(MIPSop_q), .clk(clock_1_out), .Q(register_7_q));  // open: en, clr
  Register #(.width(1)) EMWE (.D(wesel_1_we), .clk(clock_1_out), .Q(EMWE_q));  // open: en, clr
  nor nor_1 (nor_1_out, register_6_q[20], register_6_q[21], register_6_q[22], register_6_q[23], register_6_q[24], register_6_q[25], register_6_q[27], register_6_q[28], register_6_q[29], register_6_q[30], register_6_q[31], register_6_q[26]);
  memin memin_1 (.W(register_6_q), .store(store_q), .MIPSop(register_7_q), .A(memin_1_a), .D(memin_1_d));
  memsel memsel_1 (.W(register_6_q), .MIPSop(register_7_q), .sel(memsel_1_sel), .str(memsel_1_str), .ld(memsel_1_ld));
  and and_1 (and_1_out, EMWE_q, nor_1_out);
  // MIPS_RAM mips_ram_1: pin names not known; wires that end beside it: memin_1_a, memin_1_d, memsel_1_str, memsel_1_sel, clock_1_out, memsel_1_ld, mips_ram_1_p7
  Multiplexer #(.enable("false")) multiplexer_7 (
    .in0(EMWE_q), .in1(and_1_out), .out(multiplexer_7_out), .sel(memsel_1_ld));
  loadsel loadsel_1 (
    .non_lw(register_6_q), .D(mips_ram_1_p7), .MIPSop(register_7_q), .adr01(register_6_q[1:0]),
    .W(loadsel_1_w));
  Register #(.width(32)) register_8 (.D(loadsel_1_w), .clk(clock_1_out), .Q(registerfile_1_p1));  // open: en, clr
  Register #(.width(5)) MWrd (.D(EMrd_q), .clk(clock_1_out), .Q(registerfile_1_p4));  // open: en, clr
  Register #(.width(1)) MWWE (.D(multiplexer_7_out), .clk(clock_1_out), .Q(registerfile_1_p3));  // open: en, clr

  // Notes on the sheet:
  //   contents of mipsprogramrom_1 (hex, n*v repeats v):
  //   ANDI $2, $1, 346 ORI $3, $2, 25 XORI $1, $1, 45 SLTI $2, $3, -348 SLTIU $3, $3, 348 LUI $2, 764 ADDU
  //   $3, $1, $2 SUBU $2, $3, $2 AND $1, $2, $3 OR $3, $1, $2 XOR $2, $3, $2 NOR $1, $2, $3 SLT $2, $1, $3
  //   MOVZ $1, $3, $2 SLTU $2, $1, $3 MOVN $1, $3, $2 MOVZ $1, $3, $2 SLL $2, $1, 2 SRL $3, $1, 5 SRA $3,
  //   $2, 2 SLLV $2, $1, $3 SRLV $1, $3, $2 SRAV $3, $1, $2
endmodule

module JandB (
  input  [31:0] PC,
  input  [31:0] signedoff,
  input  [31:0] rs,
  input  Branch,
  input  [31:0] MIPSop,
  input  stalling,
  input  OldJ,
  input  WE,
  output [31:0] NPC,
  output J
);

  wire not_2_out, not_3_out, or_1_out, or_2_out, pcsel_1_s0, pcsel_1_s1;
  wire [1:0] and_2_out;
  wire [2:2] not_1_out;
  wire [29:0] incrementer_1_p2;
  wire [31:0] adder_1_out, bit_extender_1_out, multiplexer_1_out, multiplexer_2_out, subtractor_1_out;

  not not_1 (not_1_out[2], MIPSop[30]);
  not not_2 (not_2_out, OldJ);
  assign bit_extender_1_out = {{29{1'b0}}, {not_1_out[2], {2{MIPSop[30]}}}};  // Bit_Extender bit_extender_1
  Subtractor #(.width(32)) subtractor_1 (.a(PC), .b(bit_extender_1_out), .out(subtractor_1_out));  // open: bin, bout
  // Incrementer #(.width(30)) incrementer_1: pin names not known; wires that end beside it: PC[31:2], incrementer_1_p2
  Adder #(.width(32)) adder_1 (
    .a(subtractor_1_out), .b({signedoff[29:0], {2{MIPSop[30]}}}), .out(adder_1_out));  // open: cin, cout
  PCsel pcsel_1 (
    .branch(Branch), .op31(MIPSop[31]), .op30(MIPSop[30]), .op29(MIPSop[29]), .op28(MIPSop[28]),
    .op27(MIPSop[27]), .op26(MIPSop[26]), .op5(MIPSop[5]), .op3(MIPSop[3]), .op1(MIPSop[1]), .s1(pcsel_1_s1),
    .s0(pcsel_1_s0));
  Multiplexer #(.select(2), .width(32), .enable("false")) multiplexer_1 (
    .in0({incrementer_1_p2, PC[1:0]}), .in1(adder_1_out), .in2(rs),
    .in3({subtractor_1_out[31:28], MIPSop[25:0], {2{MIPSop[30]}}}), .out(multiplexer_1_out), .sel(and_2_out));
  and and_1 (and_2_out[1], not_2_out, pcsel_1_s1);
  and and_2 (and_2_out[0], pcsel_1_s0, not_2_out);
  or or_1 (or_1_out, PC[31], PC[30], PC[29], PC[28], PC[27], PC[26], PC[25], PC[24], PC[23], PC[22], PC[21], PC[20], PC[19], PC[18], PC[17], PC[16], PC[15], PC[14], PC[13], PC[12], PC[11], PC[10], PC[9], PC[8], PC[7], PC[6], PC[5], PC[4], PC[3]);
  Multiplexer #(.width(32), .enable("false")) multiplexer_2 (
    .in0({incrementer_1_p2, PC[1:0]}), .in1(multiplexer_1_out), .out(multiplexer_2_out), .sel(or_1_out));
  or or_2 (or_2_out, and_2_out[0], and_2_out[1]);
  not not_3 (not_3_out, stalling);
  and and_3 (J, or_1_out, or_2_out, not_3_out);
  Multiplexer #(.width(32), .enable("false")) multiplexer_3 (
    .in0(multiplexer_2_out), .in1(PC), .out(NPC), .sel(stalling));
endmodule

module control (
  input  [31:0] MIPSop,
  output [4:0] rB,
  output [4:0] rA,
  output [4:0] rW
);

  wire nor_1_out, not_1_out, not_2_out, or_1_out;
  wire [4:0] multiplexer_1_out;

  or or_1 (or_1_out, MIPSop[29], MIPSop[31]);
  Multiplexer #(.width(5), .enable("false")) multiplexer_1 (
    .in0(MIPSop[15:11]), .in1(MIPSop[20:16]), .out(multiplexer_1_out), .sel(or_1_out));
  Multiplexer #(.width(5), .enable("false")) multiplexer_2 (
    .in0(multiplexer_1_out), .in1({5{MIPSop[26]}}), .out(rW), .sel(nor_1_out));
  nor nor_1 (nor_1_out, not_2_out, not_1_out, MIPSop[28], MIPSop[29], MIPSop[30], MIPSop[31]);
  not not_1 (not_1_out, MIPSop[27]);
  not not_2 (not_2_out, MIPSop[26]);

  assign rA = MIPSop[25:21];
  assign rB = MIPSop[20:16];
endmodule

module ALUdecode (
  input  [31:0] MIPSop,
  output [3:0] ALUop
);

  wire nor_1_out;
  wire [3:0] idecode_1_aluop, multiplexer_1_out, rdecode_1_aluop;
  wire [3:2] not_1_out;

  Rdecode rdecode_1 (.op05(MIPSop[5:0]), .ALUop(rdecode_1_aluop));
  nor nor_1 (nor_1_out, MIPSop[26], MIPSop[27], MIPSop[28], MIPSop[30], MIPSop[31], MIPSop[29]);
  Idecode idecode_1 (.op3126(MIPSop[31:26]), .ALUop(idecode_1_aluop));
  Multiplexer #(.width(4), .enable("false")) multiplexer_1 (
    .in0(idecode_1_aluop), .in1(rdecode_1_aluop), .out(multiplexer_1_out), .sel(nor_1_out));
  Multiplexer #(.width(4), .enable("false")) multiplexer_2 (
    .in0(multiplexer_1_out), .in1({not_1_out, {2{MIPSop[31]}}}), .out(ALUop), .sel(MIPSop[31]));
  not not_1 (not_1_out[2], MIPSop[31]);
  not not_2 (not_1_out[3], MIPSop[31]);
endmodule

module stall (
  input  [31:0] MIPSop,
  input  [4:0] FDrs,
  input  [4:0] IErt,
  input  [4:0] FDrt,
  output stalling
);

  wire and_1_out, and_2_out, and_3_out, not_1_out, or_1_out, or_2_out;
  wire [4:0] xnor_1_out, xnor_2_out;

  not not_1 (not_1_out, MIPSop[29]);
  and and_1 (and_1_out, not_1_out, MIPSop[31]);
  assign xnor_1_out = ~(FDrs ^ IErt);  // XNOR_Gate xnor_1, 5 bits wide
  assign xnor_2_out = ~(IErt ^ FDrt);  // XNOR_Gate xnor_2, 5 bits wide
  and and_2 (and_2_out, xnor_1_out[0], xnor_1_out[1], xnor_1_out[2], xnor_1_out[3], xnor_1_out[4]);
  and and_3 (and_3_out, xnor_2_out[0], xnor_2_out[1], xnor_2_out[2], xnor_2_out[3], xnor_2_out[4]);
  or or_1 (or_1_out, IErt[0], IErt[1], IErt[2], IErt[3], IErt[4]);
  or or_2 (or_2_out, and_2_out, and_3_out);
  and and_4 (stalling, and_1_out, or_2_out, or_1_out);
endmodule

module EXhazard (
  input  EMWE,
  input  [4:0] EMrd,
  input  [4:0] IErs,
  input  [4:0] IErt,
  output FA,
  output FB
);

  wire and_1_out, and_2_out, or_1_out;
  wire [4:0] xnor_1_out, xnor_2_out;

  or or_1 (or_1_out, EMrd[0], EMrd[1], EMrd[2], EMrd[3], EMrd[4]);
  assign xnor_1_out = ~(EMrd ^ IErs);  // XNOR_Gate xnor_1, 5 bits wide
  assign xnor_2_out = ~(EMrd ^ IErt);  // XNOR_Gate xnor_2, 5 bits wide
  and and_1 (and_1_out, xnor_1_out[0], xnor_1_out[1], xnor_1_out[2], xnor_1_out[3], xnor_1_out[4]);
  and and_2 (and_2_out, xnor_2_out[0], xnor_2_out[1], xnor_2_out[2], xnor_2_out[3], xnor_2_out[4]);
  and and_3 (FA, EMWE, or_1_out, and_1_out);
  and and_4 (FB, EMWE, or_1_out, and_2_out);
endmodule

module MEMhazard (
  input  MWWE,
  input  [4:0] MWrd,
  input  [4:0] IErs,
  input  [4:0] IErt,
  input  EMWE,
  input  [4:0] EMrd,
  output FA,
  output FB
);

  wire and_1_out, and_2_out, and_3_out, and_4_out, and_5_out, and_6_out, and_7_out, not_1_out, not_2_out,
       or_1_out, or_2_out;
  wire [4:0] xnor_1_out, xnor_2_out, xnor_3_out, xnor_4_out;

  or or_1 (or_1_out, MWrd[0], MWrd[1], MWrd[2], MWrd[3], MWrd[4]);
  assign xnor_1_out = ~(MWrd ^ IErs);  // XNOR_Gate xnor_1, 5 bits wide
  assign xnor_2_out = ~(MWrd ^ IErt);  // XNOR_Gate xnor_2, 5 bits wide
  assign xnor_3_out = ~(IErt ^ EMrd);  // XNOR_Gate xnor_3, 5 bits wide
  assign xnor_4_out = ~(IErs ^ EMrd);  // XNOR_Gate xnor_4, 5 bits wide
  or or_2 (or_2_out, EMrd[0], EMrd[1], EMrd[2], EMrd[3], EMrd[4]);
  and and_1 (and_1_out, MWWE, or_1_out);
  and and_2 (and_2_out, xnor_1_out[0], xnor_1_out[1], xnor_1_out[2], xnor_1_out[3], xnor_1_out[4]);
  and and_3 (and_3_out, xnor_2_out[0], xnor_2_out[1], xnor_2_out[2], xnor_2_out[3], xnor_2_out[4]);
  and and_4 (and_4_out, xnor_3_out[0], xnor_3_out[1], xnor_3_out[2], xnor_3_out[3], xnor_3_out[4]);
  and and_5 (and_5_out, xnor_4_out[0], xnor_4_out[1], xnor_4_out[2], xnor_4_out[3], xnor_4_out[4]);
  and and_6 (and_6_out, EMWE, and_5_out, or_2_out);
  not not_1 (not_1_out, and_6_out);
  and and_7 (and_7_out, and_4_out, EMWE, or_2_out);
  not not_2 (not_2_out, and_7_out);
  and and_8 (FA, and_1_out, and_2_out, not_1_out);
  and and_9 (FB, and_1_out, and_3_out, not_2_out);
endmodule

module ALU (
  input  [31:0] A,
  input  [31:0] B,
  input  [3:0] op,
  input  [31:0] imme,
  input  [4:0] shamt,
  input  [31:0] MIPSop,
  input  [31:0] PC,
  output [31:0] C,
  output [31:0] W
);

  wire and_1_out, and_2_out, and_3_out, comparator_1_lt, comparator_2_lt, nor_1_out, nor_2_out, not_1_out,
       not_2_out, not_3_out, not_4_out, not_6_out, not_7_out, not_8_out, not_9_out, not_10_out, or_1_out,
       or_2_out, or_3_out;
  wire [1:0] rsel1_1_sb0, rsel2_1_sb0;
  wire [4:0] multiplexer_1_out, multiplexer_2_out;
  wire [4:4] not_5_out;
  wire [29:0] incrementer_1_p2;
  wire [31:0] bit_extender_1_out, bit_extender_2_out, bit_extender_3_out, bit_extender_4_out, mips_alu_1_p5,
       multiplexer_3_out, multiplexer_4_out, multiplexer_5_out, multiplexer_6_out, multiplexer_7_out;

  Multiplexer #(.width(5), .enable("false")) multiplexer_1 (
    .in0(shamt), .in1(A[4:0]), .out(multiplexer_1_out), .sel(MIPSop[2]));
  not not_1 (not_1_out, MIPSop[5]);
  assign bit_extender_1_out = {{31{MIPSop[30]}}, MIPSop[30]};  // Bit_Extender bit_extender_1
  Multiplexer #(.width(5), .enable("false")) multiplexer_2 (
    .in0(multiplexer_1_out), .in1({not_5_out[4], {4{MIPSop[30]}}}), .out(multiplexer_2_out), .sel(and_1_out));
  and and_1 (and_1_out, MIPSop[26], MIPSop[27], MIPSop[28], MIPSop[29], not_3_out, not_2_out);
  not not_2 (not_2_out, MIPSop[31]);
  not not_3 (not_3_out, MIPSop[30]);
  // Incrementer #(.width(30)) incrementer_1: pin names not known; wires that end beside it: PC[31:2], incrementer_1_p2
  not not_4 (not_4_out, MIPSop[29]);
  and and_2 (and_2_out, not_1_out, MIPSop[3], not_4_out);
  Multiplexer #(.width(32), .enable("false")) multiplexer_3 (
    .in0(A), .in1(bit_extender_1_out), .out(multiplexer_3_out), .sel(and_2_out));
  Multiplexer #(.width(32), .enable("false")) multiplexer_4 (
    .in0(B), .in1(imme), .out(multiplexer_4_out), .sel(or_1_out));
  or or_1 (or_1_out, MIPSop[31], MIPSop[29]);
  not not_5 (not_5_out[4], MIPSop[30]);
  // Mips_ALU mips_alu_1: pin names not known; wires that end beside it: multiplexer_3_out, multiplexer_4_out, op, multiplexer_2_out, mips_alu_1_p5
  Comparator #(.width(32), .mode("unsigned")) comparator_1 (
    .a(multiplexer_3_out), .b(multiplexer_4_out), .lt(comparator_1_lt));  // open: gt, eq
  Comparator #(.width(32)) comparator_2 (
    .a(multiplexer_3_out), .b(multiplexer_4_out), .lt(comparator_2_lt));  // open: gt, eq
  assign bit_extender_2_out = {{31{1'b0}}, comparator_1_lt};  // Bit_Extender bit_extender_2
  assign bit_extender_3_out = {{31{1'b0}}, comparator_2_lt};  // Bit_Extender bit_extender_3
  rsel1 rsel1_1 (.op5(MIPSop[5]), .op3(MIPSop[3]), .op0(MIPSop[0]), .sb1(rsel1_1_sb0[1]), .sb0(rsel1_1_sb0[0]));
  rsel2 rsel2_1 (
    .op28(MIPSop[28]), .op27(MIPSop[27]), .op26(MIPSop[26]), .op31(MIPSop[31]), .sb1(rsel2_1_sb0[1]),
    .sb0(rsel2_1_sb0[0]));
  Multiplexer #(.select(2), .width(32), .enable("false")) multiplexer_5 (
    .in0(A), .in1(mips_alu_1_p5), .in2(bit_extender_3_out), .in3(bit_extender_2_out),
    .out(multiplexer_5_out), .sel(rsel1_1_sb0));
  Multiplexer #(.select(2), .width(32), .enable("false")) multiplexer_6 (
    .in0(A), .in1(mips_alu_1_p5), .in2(bit_extender_3_out), .in3(bit_extender_2_out),
    .out(multiplexer_6_out), .sel(rsel2_1_sb0));
  assign bit_extender_4_out = {{31{1'b0}}, MIPSop[0]};  // Bit_Extender bit_extender_4
  and and_3 (and_3_out, MIPSop[0], not_6_out);
  Multiplexer #(.width(32), .enable("false")) multiplexer_7 (
    .in0(multiplexer_5_out), .in1(multiplexer_6_out), .out(multiplexer_7_out), .sel(or_2_out));
  or or_2 (or_2_out, MIPSop[29], MIPSop[31]);
  Multiplexer #(.width(32), .enable("false")) multiplexer_8 (
    .in0(mips_alu_1_p5), .in1(bit_extender_4_out), .out(C), .sel(and_3_out));
  not not_6 (not_6_out, MIPSop[1]);
  Multiplexer #(.width(32), .enable("false")) multiplexer_9 (
    .in0(multiplexer_7_out), .in1({incrementer_1_p2, PC[1:0]}), .out(W), .sel(or_3_out));
  or or_3 (or_3_out, nor_1_out, nor_2_out);
  nor nor_1 (nor_1_out, MIPSop[31], MIPSop[30], MIPSop[29], not_8_out, not_7_out, MIPSop[28]);
  not not_7 (not_7_out, MIPSop[26]);
  not not_8 (not_8_out, MIPSop[27]);
  nor nor_2 (nor_2_out, MIPSop[31], MIPSop[30], MIPSop[29], MIPSop[28], MIPSop[27], MIPSop[26], MIPSop[5], not_10_out, MIPSop[1], not_9_out);
  not not_9 (not_9_out, MIPSop[0]);
  not not_10 (not_10_out, MIPSop[3]);
endmodule

module Branch (
  input  [31:0] A,
  input  [31:0] B,
  input  [31:0] MIPSop,
  output Branch
);

  wire and_1_out, and_2_out, branchsel_1_eq, branchsel_1_ge, branchsel_1_le, comparator_1_gt,
       comparator_2_eq, comparator_3_lt, multiplexer_2_out, multiplexer_3_out, multiplexer_4_out, not_1_out,
       not_2_out, xor_1_out;
  wire [31:0] bit_extender_1_out, multiplexer_1_out;

  assign bit_extender_1_out = {{31{1'b0}}, MIPSop[30]};  // Bit_Extender bit_extender_1
  Multiplexer #(.width(32), .enable("false")) multiplexer_1 (
    .in0(bit_extender_1_out), .in1(B), .out(multiplexer_1_out), .sel(and_1_out));
  and and_1 (and_1_out, MIPSop[28], not_1_out);
  not not_1 (not_1_out, MIPSop[27]);
  BranchSel branchsel_1 (
    .op16(MIPSop[16]), .op26(MIPSop[26]), .op27(MIPSop[27]), .op28(MIPSop[28]), .eq(branchsel_1_eq),
    .ge(branchsel_1_ge), .le(branchsel_1_le));
  Multiplexer #(.enable("false")) multiplexer_2 (
    .in0(MIPSop[30]), .in1(comparator_1_gt), .out(multiplexer_2_out), .sel(branchsel_1_ge));
  Comparator #(.width(32)) comparator_1 (.a(A), .b(multiplexer_1_out), .gt(comparator_1_gt));  // open: eq, lt
  Comparator #(.width(32)) comparator_2 (.a(A), .b(multiplexer_1_out), .eq(comparator_2_eq));  // open: gt, lt
  and and_2 (and_2_out, MIPSop[26], not_2_out, MIPSop[28]);
  not not_2 (not_2_out, MIPSop[27]);
  Comparator #(.width(32)) comparator_3 (.a(A), .b(multiplexer_1_out), .lt(comparator_3_lt));  // open: gt, eq
  xor xor_1 (xor_1_out, comparator_2_eq, and_2_out);
  Multiplexer #(.enable("false")) multiplexer_3 (
    .in0(MIPSop[30]), .in1(comparator_3_lt), .out(multiplexer_3_out), .sel(branchsel_1_le));
  Multiplexer #(.enable("false")) multiplexer_4 (
    .in0(MIPSop[30]), .in1(xor_1_out), .out(multiplexer_4_out), .sel(branchsel_1_eq));
  or or_1 (Branch, multiplexer_2_out, multiplexer_4_out, multiplexer_3_out);
endmodule

module WEsel (
  input  [31:0] C,
  input  [31:0] MIPSop,
  input  stalling,
  input  J,
  output WE
);

  wire and_1_out, and_2_out, and_3_out, multiplexer_1_out, multiplexer_2_out, nor_1_out, not_1_out,
       not_2_out, not_3_out, not_4_out;

  nor nor_1 (nor_1_out, MIPSop[29], MIPSop[31], MIPSop[30], MIPSop[28], MIPSop[27], MIPSop[26]);
  not not_1 (not_1_out, MIPSop[30]);
  Multiplexer #(.enable("false")) multiplexer_1 (.in0(not_1_out), .in1(C[0]), .out(multiplexer_1_out), .sel(and_1_out));
  and and_1 (and_1_out, nor_1_out, MIPSop[3], not_2_out);
  not not_2 (not_2_out, MIPSop[5]);
  Multiplexer #(.enable("false")) multiplexer_2 (
    .in0(multiplexer_1_out), .in1(not_3_out), .out(multiplexer_2_out), .sel(and_2_out));
  not not_3 (not_3_out, MIPSop[31]);
  and and_2 (and_2_out, MIPSop[31], MIPSop[29]);
  and and_3 (and_3_out, multiplexer_2_out, not_4_out);
  not not_4 (not_4_out, J);
  Multiplexer #(.enable("false")) multiplexer_3 (.in0(and_3_out), .in1(MIPSop[30]), .out(WE), .sel(stalling));
endmodule

module memsel (
  input  [31:0] W,
  input  [31:0] MIPSop,
  output [3:0] sel,
  output str,
  output ld
);

  wire and_7_out, nor_1_out, not_1_out, not_2_out, not_3_out, not_4_out, not_5_out;
  wire [3:0] and_1_out, bit_extender_1_out;

  not not_1 (not_1_out, W[0]);
  and and_1 (and_1_out[0], not_1_out, not_2_out);
  not not_2 (not_2_out, W[1]);
  and and_2 (and_1_out[1], W[0], not_3_out);
  not not_3 (not_3_out, W[1]);
  not not_4 (not_4_out, W[0]);
  and and_3 (and_1_out[2], not_4_out, W[1]);
  and and_4 (and_1_out[3], W[0], W[1]);
  nor nor_1 (nor_1_out, W[20], W[21], W[22], W[23], W[24], W[25], W[27], W[28], W[29], W[30], W[31], W[26]);
  assign bit_extender_1_out = {{3{MIPSop[26]}}, MIPSop[26]};  // Bit_Extender bit_extender_1
  and and_5 (str, MIPSop[29], nor_1_out, MIPSop[31]);
  not not_5 (not_5_out, MIPSop[29]);
  and and_6 (ld, not_5_out, MIPSop[31]);
  Multiplexer #(.width(4), .enable("false")) multiplexer_1 (
    .in0(and_1_out), .in1(bit_extender_1_out), .out(sel), .sel(and_7_out));
  and and_7 (and_7_out, MIPSop[26], MIPSop[27]);
endmodule

module memin (
  input  [31:0] W,
  input  [31:0] store,
  input  [31:0] MIPSop,
  output [19:0] A,
  output [31:0] D
);

  wire and_1_out, and_2_out, and_3_out, and_4_out, not_1_out, not_2_out, not_3_out, not_4_out;
  wire [7:0] bit_extender_1_out, multiplexer_1_out, multiplexer_2_out, multiplexer_3_out, multiplexer_4_out;

  assign bit_extender_1_out = {{7{1'b0}}, MIPSop[30]};  // Bit_Extender bit_extender_1
  not not_1 (not_1_out, W[0]);
  and and_1 (and_1_out, not_1_out, not_2_out);
  not not_2 (not_2_out, W[1]);
  and and_2 (and_2_out, W[0], not_3_out);
  not not_3 (not_3_out, W[1]);
  not not_4 (not_4_out, W[0]);
  and and_3 (and_3_out, not_4_out, W[1]);
  and and_4 (and_4_out, W[0], W[1]);
  Multiplexer #(.width(8), .enable("false")) multiplexer_1 (
    .in0(bit_extender_1_out), .in1(store[7:0]), .out(multiplexer_1_out), .sel(and_1_out));
  Multiplexer #(.width(8), .enable("false")) multiplexer_2 (
    .in0(bit_extender_1_out), .in1(store[7:0]), .out(multiplexer_2_out), .sel(and_2_out));
  Multiplexer #(.width(8), .enable("false")) multiplexer_3 (
    .in0(bit_extender_1_out), .in1(store[7:0]), .out(multiplexer_3_out), .sel(and_3_out));
  Multiplexer #(.width(8), .enable("false")) multiplexer_4 (
    .in0(bit_extender_1_out), .in1(store[7:0]), .out(multiplexer_4_out), .sel(and_4_out));
  Multiplexer #(.width(32), .enable("false")) multiplexer_5 (
    .in0({multiplexer_4_out, multiplexer_3_out, multiplexer_2_out, multiplexer_1_out}), .in1(store), .out(D),
    .sel(MIPSop[26]));

  assign A = {W[19:2], {2{MIPSop[30]}}};
endmodule

module loadsel (
  input  [31:0] non_lw,
  input  [31:0] D,
  input  [31:0] MIPSop,
  input  [1:0] adr01,
  output [31:0] W
);

  wire and_1_out, and_2_out, not_1_out;
  wire [7:0] multiplexer_1_out;
  wire [31:0] bit_extender_1_out, bit_extender_2_out, multiplexer_2_out, multiplexer_3_out;

  Multiplexer #(.select(2), .width(8), .enable("false")) multiplexer_1 (
    .in0(D[7:0]), .in1(D[15:8]), .in2(D[23:16]), .in3(D[31:24]), .out(multiplexer_1_out), .sel(adr01));
  assign bit_extender_1_out = {{24{multiplexer_1_out[7]}}, multiplexer_1_out};  // Bit_Extender bit_extender_1
  assign bit_extender_2_out = {{24{1'b0}}, multiplexer_1_out};  // Bit_Extender bit_extender_2
  Multiplexer #(.width(32), .enable("false")) multiplexer_2 (
    .in0(bit_extender_1_out), .in1(bit_extender_2_out), .out(multiplexer_2_out), .sel(MIPSop[28]));
  and and_1 (and_1_out, MIPSop[26], MIPSop[27]);
  and and_2 (and_2_out, MIPSop[31], not_1_out);
  Multiplexer #(.width(32), .enable("false")) multiplexer_3 (
    .in0(multiplexer_2_out), .in1(D), .out(multiplexer_3_out), .sel(and_1_out));
  Multiplexer #(.width(32), .enable("false")) multiplexer_4 (
    .in0(non_lw), .in1(multiplexer_3_out), .out(W), .sel(and_2_out));
  not not_1 (not_1_out, MIPSop[29]);
endmodule

module rsel1 (
  input  op5,
  input  op3,
  input  op0,
  output sb1,
  output sb0
);

  wire and_2_out, not_1_out;

  and and_1 (sb1, op5, op3);
  not not_1 (not_1_out, op3);
  and and_2 (and_2_out, op5, op0);
  or or_1 (sb0, not_1_out, and_2_out);
endmodule

module rsel2 (
  input  op28,
  input  op27,
  input  op26,
  input  op31,
  output sb1,
  output sb0
);

  wire not_1_out, not_2_out;

  not not_1 (not_1_out, op28);
  and and_1 (sb1, not_1_out, op27, not_2_out);
  not not_2 (not_2_out, op31);
  or or_1 (sb0, op31, op26, op28);
endmodule

module Idecode (
  input  [5:0] op3126,
  output [3:0] ALUop
);

  wire and_1_out, not_1_out, not_2_out, not_3_out, not_4_out;

  not not_1 (not_1_out, op3126[1]);
  not not_2 (not_2_out, op3126[0]);
  not not_3 (not_3_out, op3126[1]);
  not not_4 (not_4_out, op3126[0]);
  and and_1 (and_1_out, op3126[2], not_1_out);
  and and_2 (ALUop[2], op3126[1], not_2_out);
  and and_3 (ALUop[1], not_3_out, op3126[0]);
  or or_1 (ALUop[3], not_4_out, and_1_out);

  assign ALUop[0] = op3126[4];
endmodule

module Rdecode (
  input  [5:0] op05,
  output [3:0] ALUop
);

  wire and_1_out, and_2_out, and_3_out, and_5_out, not_1_out, not_2_out;

  and and_1 (and_1_out, op05[5], op05[2]);
  not not_1 (not_1_out, op05[3]);
  and and_2 (and_2_out, op05[3], op05[0]);
  and and_3 (and_3_out, op05[5], op05[0]);
  not not_2 (not_2_out, op05[5]);
  or or_1 (ALUop[3], op05[3], and_1_out);
  and and_4 (ALUop[2], not_1_out, op05[1]);
  or or_2 (ALUop[1], and_2_out, and_3_out);
  and and_5 (and_5_out, not_2_out, op05[0]);
  or or_3 (ALUop[0], and_5_out, op05[3]);
endmodule

module BranchSel (
  input  op16,
  input  op26,
  input  op27,
  input  op28,
  output eq,
  output ge,
  output le
);

  wire and_1_out, and_2_out, and_3_out, and_4_out, and_5_out, not_1_out, not_2_out, not_3_out, not_4_out,
       not_5_out, not_6_out;

  not not_1 (not_1_out, op26);
  not not_2 (not_2_out, op27);
  and and_1 (and_1_out, not_2_out, op28);
  and and_2 (and_2_out, op26, op27);
  and and_3 (and_3_out, op16, not_3_out);
  not not_3 (not_3_out, op28);
  not not_4 (not_4_out, op16);
  and and_4 (and_4_out, not_4_out, not_5_out);
  not not_5 (not_5_out, op28);
  not not_6 (not_6_out, op26);
  and and_5 (and_5_out, not_6_out, op27);
  or or_1 (eq, not_1_out, and_1_out, op16);
  or or_2 (ge, and_2_out, and_3_out);
  or or_3 (le, and_4_out, and_5_out);
endmodule

module PCsel (
  input  branch,
  input  op31,
  input  op30,
  input  op29,
  input  op28,
  input  op27,
  input  op26,
  input  op5,
  input  op3,
  input  op1,
  output s1,
  output s0
);

  wire and_1_out, and_2_out, and_3_out, and_4_out, and_5_out, and_6_out, not_1_out, not_2_out, not_3_out,
       not_4_out, not_5_out, not_6_out, not_7_out, not_8_out, not_9_out, not_10_out, not_11_out, not_12_out,
       not_13_out, not_14_out, not_15_out, not_16_out, not_17_out, not_18_out, not_19_out, not_20_out,
       not_21_out, not_22_out, not_23_out, not_24_out, not_25_out, not_26_out;

  not not_1 (not_1_out, op31);
  not not_2 (not_2_out, op30);
  not not_3 (not_3_out, op29);
  not not_4 (not_4_out, op28);
  not not_5 (not_5_out, op26);
  not not_6 (not_6_out, op5);
  not not_7 (not_7_out, op1);
  not not_8 (not_8_out, op31);
  not not_9 (not_9_out, op30);
  not not_10 (not_10_out, op29);
  not not_11 (not_11_out, op28);
  not not_12 (not_12_out, op31);
  not not_13 (not_13_out, op30);
  not not_14 (not_14_out, op28);
  not not_15 (not_15_out, op27);
  not not_16 (not_16_out, op26);
  not not_17 (not_17_out, op31);
  not not_18 (not_18_out, op30);
  not not_19 (not_19_out, op29);
  not not_20 (not_20_out, op31);
  not not_21 (not_21_out, op30);
  not not_22 (not_22_out, op29);
  not not_23 (not_23_out, op28);
  not not_24 (not_24_out, op31);
  not not_25 (not_25_out, op30);
  not not_26 (not_26_out, op29);
  and and_1 (and_1_out, not_1_out, not_2_out, not_3_out, not_4_out, not_5_out, not_6_out, op3, not_7_out);
  and and_2 (and_2_out, not_8_out, not_9_out, not_10_out, not_11_out, op27);
  and and_3 (and_3_out, not_12_out, not_13_out, op29, not_14_out, not_15_out, not_16_out);
  and and_4 (and_4_out, not_17_out, not_18_out, not_19_out, op26, branch);
  and and_5 (and_5_out, not_20_out, not_21_out, not_22_out, not_23_out, op27);
  and and_6 (and_6_out, not_24_out, not_25_out, not_26_out, op28, branch);
  or or_1 (s1, and_1_out, and_2_out, and_3_out);
  or or_2 (s0, and_4_out, and_5_out, and_6_out);
endmodule
